# Fritzing sketch Drums Schematic_img (saved by Fritzing 0.9.3b)
breadboards: 1

parts:
  Part1 = Arduino Uno (Rev3)
  J1 = Piezo Speaker
  J2 = Piezo Speaker
  J3 = Piezo Speaker
  J4 = Piezo Speaker
  J5 = Piezo Speaker
  J6 = Piezo Speaker
  SD_card_module1 = SD Card Module
  SP1 = SPEAKER [package=pcb_mount_speaker]

nets:
  N1: Part1.A0, J6.pin2
  N2: Part1.A1, J5.pin2
  N3: Part1.A2, J4.pin2
  N4: Part1.A3, J3.pin2
  N5: Part1.A4/SDA, J2.pin2
  N6: Part1.A5/SCL, J1.pin2
  N7: Part1.D9_PWM, SP1.-
  N8: Part1.D11_PWM/MOSI, SD_card_module1.MOSI
  N9: Part1.D12/MISO, SD_card_module1.MISO
  N10: Part1.D13/SCK, SD_card_module1.SCK
  GND: Part1.GND, J1.pin1, J2.pin1, J3.pin1, J4.pin1, J5.pin1, J6.pin1, SD_card_module1.GND, SP1.+
  N11: Part1.D4, SD_card_module1.CS
  N12: Part1.3V3, SD_card_module1.+3.3
  N13: Part1.5V, SD_card_module1.+5

custom parts:
  SD Card Module: SD Card Module Slot Socket Reader For Arduino ARM MCU
